// Digital circuit controller.dig as structural Verilog
module controller (
  input  rst,
  input  zero,
  input  clk,
  input  beginn,
  input  reset,
  input  endd,
  output load,
  output start,
  output countdown
);

  wire d_ff_as_1_q, not_1_out, or_2_out;

  not not_1 (not_1_out, rst);
  or or_1 (load, not_1_out, reset);
  or or_2 (or_2_out, load, zero);
  D_FF_AS d_ff_as_1 (.Set(beginn), .D(d_ff_as_1_q), .C(clk), .Clr(or_2_out), .Q(d_ff_as_1_q));  // open: nQ
  and and_1 (countdown, d_ff_as_1_q, endd);
  or or_3 (start, beginn, countdown);
endmodule
