// Digital circuit downcounter.dig as structural Verilog
module downcounter (
  input  c1khz,
  input  [3:0] pm10,
  input  [3:0] pm1,
  input  [3:0] ps10,
  input  [3:0] ps1,
  input  load,
  input  count,
  input  rst,
  output [3:0] s1,
  output [3:0] s2,
  output [3:0] m1,
  output [3:0] m10,
  output zero
);

  wire downcounteronedigit_1_zero, downcounteronedigit_2_zero, downcounteronedigit_3_zero,
       downcounteronedigit_4_zero, or_1_out, or_2_out, or_3_out, or_4_out;
  wire [3:0] multiplexer_1_out, multiplexer_2_out, multiplexer_3_out, multiplexer_4_out;

  Multiplexer #(.Bits(4)) multiplexer_1 (.sel(load), .in_0(4'b1001), .in_1(ps1), .out(multiplexer_1_out));
  Multiplexer #(.Bits(4)) multiplexer_2 (.sel(load), .in_0(4'b0101), .in_1(ps10), .out(multiplexer_2_out));
  Multiplexer #(.Bits(4)) multiplexer_3 (.sel(load), .in_0(4'b1001), .in_1(pm1), .out(multiplexer_3_out));
  Multiplexer #(.Bits(4)) multiplexer_4 (.sel(load), .in_0(4'b1001), .in_1(pm10), .out(multiplexer_4_out));
  or or_1 (or_1_out, downcounteronedigit_1_zero, load);
  or or_2 (or_2_out, load, downcounteronedigit_2_zero);
  or or_3 (or_3_out, load, downcounteronedigit_3_zero);
  or or_4 (or_4_out, load, downcounteronedigit_4_zero);
  downcounterOneDigit downcounteronedigit_1 (
    .EN(count), .LOAD(or_1_out), .IN(multiplexer_1_out), .CLK(c1khz), .RESET(rst), .CNT(s1),
    .ZERO(downcounteronedigit_1_zero));
  downcounterOneDigit downcounteronedigit_2 (
    .EN(downcounteronedigit_1_zero), .LOAD(or_2_out), .IN(multiplexer_2_out), .CLK(c1khz), .RESET(rst),
    .CNT(s2), .ZERO(downcounteronedigit_2_zero));
  downcounterOneDigit downcounteronedigit_3 (
    .EN(downcounteronedigit_2_zero), .LOAD(or_3_out), .IN(multiplexer_3_out), .CLK(c1khz), .RESET(rst),
    .CNT(m1), .ZERO(downcounteronedigit_3_zero));
  downcounterOneDigit downcounteronedigit_4 (
    .EN(downcounteronedigit_3_zero), .LOAD(or_4_out), .IN(multiplexer_4_out), .CLK(c1khz), .RESET(rst),
    .CNT(m10), .ZERO(downcounteronedigit_4_zero));
  and and_1 (zero, downcounteronedigit_1_zero, downcounteronedigit_2_zero, downcounteronedigit_3_zero, downcounteronedigit_4_zero);
endmodule
