// Digital circuit downcounterOneDigit.dig as structural Verilog
module downcounterOneDigit (
  input  EN,
  input  LOAD,
  input  [3:0] IN,
  input  CLK,
  input  RESET,
  output [3:0] CNT,
  output ZERO
);

  wire d_ff_as_1_nq, d_ff_as_2_nq, d_ff_as_3_nq, d_ff_as_4_nq, multiplexer_1_out, multiplexer_2_out,
       multiplexer_3_out, multiplexer_4_out, not_1_out;
  wire [0:0] and_1_out, and_2_out, and_3_out;

  not not_1 (not_1_out, RESET);
  and and_1 (and_1_out[0], d_ff_as_1_nq, EN);
  and and_2 (and_2_out[0], d_ff_as_2_nq, and_1_out[0]);
  and and_3 (and_3_out[0], and_2_out[0], d_ff_as_3_nq);
  Multiplexer #(.Selector_Bits(2)) multiplexer_1 (
    .sel({LOAD, EN}), .in_0(CNT[0]), .in_1(d_ff_as_1_nq), .in_2(IN[0]), .in_3(IN[0]), .out(multiplexer_1_out));
  Multiplexer #(.Selector_Bits(2)) multiplexer_2 (
    .sel({LOAD, and_1_out[0]}), .in_0(CNT[1]), .in_1(d_ff_as_2_nq), .in_2(IN[1]), .in_3(IN[1]),
    .out(multiplexer_2_out));
  Multiplexer #(.Selector_Bits(2)) multiplexer_3 (
    .sel({LOAD, and_2_out[0]}), .in_0(CNT[2]), .in_1(d_ff_as_3_nq), .in_2(IN[2]), .in_3(IN[2]),
    .out(multiplexer_3_out));
  Multiplexer #(.Selector_Bits(2)) multiplexer_4 (
    .sel({LOAD, and_3_out[0]}), .in_0(CNT[3]), .in_1(d_ff_as_4_nq), .in_2(IN[3]), .in_3(IN[3]),
    .out(multiplexer_4_out));
  D_FF_AS d_ff_as_1 (.Set(1'b0), .D(multiplexer_1_out), .C(CLK), .Clr(not_1_out), .Q(CNT[0]), .nQ(d_ff_as_1_nq));
  D_FF_AS d_ff_as_2 (.Set(1'b0), .D(multiplexer_2_out), .C(CLK), .Clr(not_1_out), .Q(CNT[1]), .nQ(d_ff_as_2_nq));
  D_FF_AS d_ff_as_3 (.Set(1'b0), .D(multiplexer_3_out), .C(CLK), .Clr(not_1_out), .Q(CNT[2]), .nQ(d_ff_as_3_nq));
  D_FF_AS d_ff_as_4 (.Set(1'b0), .D(multiplexer_4_out), .C(CLK), .Clr(not_1_out), .Q(CNT[3]), .nQ(d_ff_as_4_nq));
  and and_4 (ZERO, d_ff_as_4_nq, and_3_out[0]);
endmodule
