// Digital circuit eggimer.dig as structural Verilog
module eggimer (
  input  _1_kHz
);

  wire controller_1_countdown, controller_1_load, controller_1_start, downcounter_1_zero, PRESET_out,
       RST_out, START_out, u_counter_endd;
  wire [3:0] dipswitch_1_out, dipswitch_5_out, dipswitch_9_out, dipswitch_13_out, downcounter_1_m1,
       downcounter_1_m10, downcounter_1_s1, downcounter_1_s2;

  Button #(.activeLow("true")) RST (.out(RST_out));
  Seven_Seg_Hex seven_seg_hex_1 (.d(downcounter_1_m10), .dp(1'b0));
  DipSwitch dipswitch_1 (.out(dipswitch_1_out[3]));
  DipSwitch dipswitch_2 (.out(dipswitch_1_out[2]));
  DipSwitch dipswitch_3 (.out(dipswitch_1_out[1]));
  Seven_Seg_Hex seven_seg_hex_2 (.d(downcounter_1_m1), .dp(1'b1));
  downcounter downcounter_1 (
    .c1khz(_1_kHz), .pm10(dipswitch_1_out), .pm1(dipswitch_5_out), .ps10(dipswitch_9_out),
    .ps1(dipswitch_13_out), .load(controller_1_load), .count(controller_1_countdown), .rst(RST_out),
    .s1(downcounter_1_s1), .s2(downcounter_1_s2), .m1(downcounter_1_m1), .m10(downcounter_1_m10),
    .zero(downcounter_1_zero));
  DipSwitch dipswitch_4 (.out(dipswitch_1_out[0]));
  DipSwitch dipswitch_5 (.out(dipswitch_5_out[3]));
  DipSwitch dipswitch_6 (.out(dipswitch_5_out[2]));
  Seven_Seg_Hex seven_seg_hex_3 (.d(downcounter_1_s2), .dp(1'b0));
  DipSwitch dipswitch_7 (.out(dipswitch_5_out[1]));
  DipSwitch dipswitch_8 (.out(dipswitch_5_out[0]));
  DipSwitch dipswitch_9 (.out(dipswitch_9_out[3]));
  Seven_Seg_Hex seven_seg_hex_4 (.d(downcounter_1_s1), .dp(1'b0));
  DipSwitch dipswitch_10 (.out(dipswitch_9_out[2]));
  DipSwitch dipswitch_11 (.out(dipswitch_9_out[1]));
  DipSwitch dipswitch_12 (.out(dipswitch_9_out[0]));
  DipSwitch dipswitch_13 (.out(dipswitch_13_out[3]));
  DipSwitch dipswitch_14 (.out(dipswitch_13_out[2]));
  DipSwitch dipswitch_15 (.out(dipswitch_13_out[1]));
  DipSwitch dipswitch_16 (.out(dipswitch_13_out[0]));
  controller controller_1 (
    .clk(_1_kHz), .rst(RST_out), .beginn(START_out), .reset(PRESET_out), .zero(downcounter_1_zero),
    .endd(u_counter_endd), .load(controller_1_load), .start(controller_1_start),
    .countdown(controller_1_countdown));
  Button START (.out(START_out));
  Button PRESET (.out(PRESET_out));
  counter #(.applicationType("IVERILOG")) u_counter (
    .rst(RST_out), .clk(_1_kHz), .start(controller_1_start), .endd(u_counter_endd));

  // Notes on the sheet:
  //   _1_kHz: Hz: 1000
endmodule

/* Code of counter:
module counter(
    input rst,
    input clk,
    input start,
    output endd);
    
    reg [9:0] cnt;
    
    assign endd = (cnt==0);
    
    always @(posedge clk, negedge rst)
    begin
        if (~rst)
        begin
            cnt <= 0;
        end
        else
        begin
            if (start)
                cnt <= 999;
            else if (~endd)
                cnt <= cnt-1;
        end
    end // always
endmodule
*/
